# Fritzing sketch Fritzing Sketch Source File (saved by Fritzing 0.9.3b)
breadboards: 1

parts:
  R1 = Resistor [tolerance=±5% resistance=220 package=THT]
  Part1 = Arduino Uno (Rev3)
  J1 = Basic Servo
  R2 = PHOTOCELL [package=photocell]

nets:
  N1: R1.Pin_0, Part1.A0, R2.P$2
  GND: R1.Pin_1, Part1.GND, J1.gnd
  N2: Part1.D9_PWM, J1.pulse
  5V: Part1.5V, J1.vcc, R2.P$1

notes:
  GND - Green
  VCC - Orange
  GPIO - Blue
  Developed By Web Dev Fusion
  https://www.webdevfusion.com
